# Fritzing sketch POV (saved by Fritzing 0.6.3b)
breadboards: 1

parts:
  Componente1 = TinkerKit_Hall_Sensor___T000070
  Arduino1 = Arduino
  R1 = Resistor [tolerance=±5% resistance=1k package=THT]
  R2 = Resistor [tolerance=±5% resistance=1k package=THT]
  R3 = Resistor [tolerance=±5% resistance=1k package=THT]
  R4 = Resistor [tolerance=±5% resistance=1k package=THT]
  R5 = Resistor [tolerance=±5% resistance=1k package=THT]
  R6 = Resistor [tolerance=±5% resistance=1k package=THT]
  R7 = Resistor [tolerance=±5% resistance=1k package=THT]
  Q1 = NPN-Transistor [package="SOT-23 [SMD]"]
  Q2 = NPN-Transistor [package="SOT-23 [SMD]"]
  Q3 = NPN-Transistor [package="SOT-23 [SMD]"]
  Q4 = NPN-Transistor [package="SOT-23 [SMD]"]
  Q5 = NPN-Transistor [package="SOT-23 [SMD]"]
  Q6 = NPN-Transistor [package="SOT-23 [SMD]"]
  Q7 = NPN-Transistor [package="SOT-23 [SMD]"]
  R8 = Resistor [tolerance=±5% resistance=100 package=THT]
  R9 = Resistor [tolerance=±5% resistance=100 package=THT]
  R10 = Resistor [tolerance=±5% resistance=100 package=THT]
  R11 = Resistor [tolerance=±5% resistance=100 package=THT]
  R12 = Resistor [tolerance=±5% resistance=100 package=THT]
  R13 = Resistor [tolerance=±5% resistance=100 package=THT]
  R14 = Resistor [tolerance=±5% resistance=100 package=THT]
  LED1 = LED - 5mm [color="Red (633nm)" package="5 mm [THT]"]
  LED2 = LED - 5mm [color="Red (633nm)" package="5 mm [THT]"]
  LED3 = LED - 5mm [color="Red (633nm)" package="5 mm [THT]"]
  LED4 = LED - 5mm [color="Red (633nm)" package="5 mm [THT]"]
  LED5 = LED - 5mm [color="Red (633nm)" package="5 mm [THT]"]
  LED6 = LED - 5mm [color="Red (633nm)" package="5 mm [THT]"]
  LED7 = LED - 5mm [color="Red (633nm)" package="5 mm [THT]"]

nets:
  N1: Componente1.connector0, Arduino1.+5V, LED1.anode, LED2.anode, LED3.anode, LED4.anode, LED5.anode, LED6.anode, LED7.anode
  N2: Componente1.connector1, Arduino1.A1
  N3: Componente1.connector2, Arduino1.GND, Q1.1, Q2.1, Q3.1, Q4.1, Q5.1, Q6.1, Q7.1
  N4: Arduino1.D12, R7.Pin_0
  N5: Arduino1.D11, R6.Pin_0
  N6: Arduino1.D10, R5.Pin_0
  N7: Arduino1.D9, R4.Pin_0
  N8: Arduino1.D8, R3.Pin_0
  N9: Arduino1.D7, R2.Pin_0
  N10: Arduino1.D6, R1.Pin_0
  N11: R1.Pin_1, Q1.0
  N12: R2.Pin_1, Q2.0
  N13: R3.Pin_1, Q3.0
  N14: R4.Pin_1, Q4.0
  N15: R5.Pin_1, Q5.0
  N16: R6.Pin_1, Q6.0
  N17: R7.Pin_1, Q7.0
  N18: Q1.2, R8.Pin_1
  N19: Q3.2, R10.Pin_1
  N20: Q4.2, R11.Pin_1
  N21: Q5.2, R12.Pin_1
  N22: Q6.2, R13.Pin_1
  N23: Q7.2, R14.Pin_1
  N24: R8.Pin_0, LED1.cathode
  N25: R9.Pin_0, LED2.cathode
  N26: R10.Pin_0, LED3.cathode
  N27: R11.Pin_0, LED4.cathode
  N28: R12.Pin_0, LED5.cathode
  N29: R13.Pin_0, LED6.cathode
  N30: R14.Pin_0, LED7.cathode
